// Digital circuit elevador.dig as structural Verilog
module elevador (
  input  in_1,
  input  in_2,
  input  [3:0] in_3,
  input  [3:0] in_4
);

  wire u_ElevatorControl_motor_down, u_ElevatorControl_motor_stop, u_ElevatorControl_motor_up;

  ElevatorControl #(.applicationType("GHDL"), .CodeFile("C:\\Users\\dreyr\\Desktop\\workspace\\ElevadorControl.vhdl")) u_ElevatorControl (
    .clock(in_1), .reset(in_2), .call_floor(in_3), .sensor_floor(in_4),
    .motor_up(u_ElevatorControl_motor_up), .motor_down(u_ElevatorControl_motor_down),
    .motor_stop(u_ElevatorControl_motor_stop));
  LED led_1 (.in(u_ElevatorControl_motor_up));
  LED led_2 (.in(u_ElevatorControl_motor_down));
  LED led_3 (.in(u_ElevatorControl_motor_stop));
endmodule
